# Fritzing sketch PCB (saved by Fritzing 0.7.0b)
breadboards: 1

parts:
  NodeMCU = NodeMCU V1.0
  LED1 = LED - 5mm [color="Red (633nm)" package="5 mm [THT]"]
  LED2 = LED - 5mm [color="Red (633nm)" package="5 mm [THT]"]
  LED3 = LED - 5mm [color="Red (633nm)" package="5 mm [THT]"]
  R1 = Resistor [tolerance=±5% resistance=220 package=THT]
  R2 = Resistor [tolerance=±5% resistance=220 package=THT]
  R3 = Resistor [tolerance=±5% resistance=220 package=THT]
  M1 = Pushbutton [package=THT]
  M2 = Pushbutton [package=THT]
  M3 = Pushbutton [package=THT]
  Fuse1 = Fuse with Handler [part_number=Htc-15m]
  HLK-PM1 = HLK-PM01
  AC = Screw terminal - 2 pins [package=THT]
  Reset = Pushbutton [package=THT]
  J1 = screw terminal, 3 pins
  J2 = Screw terminal - 2 pins [package=THT]

nets:
  N1: NodeMCU.D0, R1.Pin_1, J1.pin3
  N2: NodeMCU.D1, R2.Pin_1, J1.pin2
  N3: NodeMCU.D2, R3.Pin_1, J1.pin1
  N4: NodeMCU.D3, Reset.leg0
  N5: NodeMCU.GND, LED1.anode, LED2.anode, LED3.anode, M1.leg1, M2.leg1, M3.leg1, HLK-PM1.-Vo, Reset.leg1, J2.pin1
  N6: NodeMCU.D5, M1.leg0
  N7: NodeMCU.D6, M2.leg0
  N8: NodeMCU.D7, M3.leg0
  N9: NodeMCU.Vin, HLK-PM1.+Vo, J2.pin2
  N10: LED1.cathode, R1.Pin_0
  N11: LED2.cathode, R2.Pin_0
  N12: LED3.cathode, R3.Pin_0
  N13: Fuse1.Connector1, HLK-PM1.AC#1
  N14: Fuse1.Connector2, AC.pin1
  N15: HLK-PM1.AC#0, AC.pin2

notes:
  By Thanakrit

custom parts:
  NodeMCU V1.0: ESP8266 based NodeMCU
